# Fritzing sketch RAspberry-dht11 (saved by Fritzing 0.9.3b)

parts:
  Raspberry_Pi_1 = Raspberry Pi 3 [part_number=RPI-3-V1.2]
  DHT11_1 = DHT11 module
  LCD2 = LCD screen
  LCM1602_IIC2 = LCM1602 IIC [part_number="LCM1602 IIC" chip_label="LCM1602 IIC" package="DIP (Dual Inline) [THT]"]

nets:
  N1: Raspberry_Pi_1.GPIO2, LCM1602_IIC2.SDA
  N2: Raspberry_Pi_1.GPIO3, LCM1602_IIC2.SCL
  N3: Raspberry_Pi_1.GPIO4, DHT11_1.DATA
  GND: Raspberry_Pi_1.GND, DHT11_1.GND, LCM1602_IIC2.GND
  VCC: Raspberry_Pi_1.5V, DHT11_1.VCC, LCM1602_IIC2.VCC
  VSS: LCD2.VSS, LCM1602_IIC2.VSS
  VDD: LCD2.VDD, LCM1602_IIC2.VDD
  N4: LCD2.V0, LCM1602_IIC2.V0
  N5: LCD2.RS, LCM1602_IIC2.RS
  N6: LCD2.R/W, LCM1602_IIC2.RW
  N7: LCD2.E, LCM1602_IIC2.E
  N8: LCD2.DB0, LCM1602_IIC2.D0
  N9: LCD2.DB1, LCM1602_IIC2.D1
  N10: LCD2.DB2, LCM1602_IIC2.D2
  N11: LCD2.DB3, LCM1602_IIC2.D3
  N12: LCD2.DB4, LCM1602_IIC2.D4
  N13: LCD2.DB5, LCM1602_IIC2.D5
  N14: LCD2.DB6, LCM1602_IIC2.D6
  N15: LCD2.DB7, LCM1602_IIC2.D7
  N16: LCD2.LED+, LCM1602_IIC2.A
  N17: LCD2.LED-, LCM1602_IIC2.K

custom parts:
  DHT11 module: DHT11 black pcb module
  LCM1602 IIC: I2C-Module to use a 1602 or 2004 LCD on with the wire.h libory Serial LCD Modul
